# Fritzing sketch 7sd (saved by Fritzing 1.0.2b)
breadboards: 1

parts:
  A1 = Arduino UNO R4 WiFi
  SparkFun_7-Segment-Display-Blue1 = SparkFun 7-Segment Serial Display-Blue [part_number=COM-11442]
  SparkFun_7-Segment-Display-Blue3 = SparkFun 7-Segment Serial Display-Blue [part_number=COM-11442]
  SparkFun_7-Segment-Display-Blue4 = SparkFun 7-Segment Serial Display-Blue [part_number=COM-11442]
  SparkFun_7-Segment-Display-Blue2 = SparkFun 7-Segment Serial Display-Blue [part_number=COM-11442]
  J1 = 14 Segment Alphanumeric [form="♀ (female)" package=THT]

nets:
  N1: A1.Pin_7, A1.Pin_19, J1.3.3V
  VCC: A1.Pin_8, A1.Pin_27, SparkFun_7-Segment-Display-Blue1.VCC, SparkFun_7-Segment-Display-Blue3.VCC, SparkFun_7-Segment-Display-Blue4.VCC, SparkFun_7-Segment-Display-Blue2.VCC
  GND: A1.Pin_9, A1.Pin_18, A1.Pin_30, A1.Pin_48, SparkFun_7-Segment-Display-Blue1.GND, SparkFun_7-Segment-Display-Blue3.GND, SparkFun_7-Segment-Display-Blue4.GND, SparkFun_7-Segment-Display-Blue2.GND, J1.Ground
  N2: A1.Pin_50, SparkFun_7-Segment-Display-Blue1.SDA, SparkFun_7-Segment-Display-Blue3.SDA, SparkFun_7-Segment-Display-Blue4.SDA, SparkFun_7-Segment-Display-Blue2.SDA
  N3: A1.Pin_51, SparkFun_7-Segment-Display-Blue1.SCL, SparkFun_7-Segment-Display-Blue3.SCL, SparkFun_7-Segment-Display-Blue4.SCL, SparkFun_7-Segment-Display-Blue2.SCL, J1.SCL, J1.SDA

custom parts:
  Arduino UNO R4 WiFi: The Arduino UNO R4 WiFi merges the RA4M1 microprocessor from Renesas with the ESP32-S3 from Espressif, creating an all-in-one tool for makers with enhanced processing power and a diverse array of new peripherals.
  SparkFun 7-Segment Serial Display-Blue: 4-digit 7-segment displays are really neat little devices, it’s a shame that they can be so cumbersome to control. Well we’ve solved that problem by making them a little bit “smarter.” The SparkFun 7-Segment Serial Display combines a classic 4-digit 7-segment display and an ATMega328 microcontroller allowing you to control every segment individually using only a few serial lines. The Serial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
  14 Segment Alphanumeric: 14 Segment Serial Alphanumeric
