# Fritzing sketch Automatic Power switch (saved by Fritzing 1.0.2b)
circuit board: 7.22467cm x 5.85419cm
breadboards: 1

parts:
  Q1 = Basic FET P-Channel [package="TO220 [THT]"]
  V1 = DC Power [voltage=9]
  V2 = DC Power [voltage=9.6]
  C1 = Electrolytic Capacitor [capacitance=100µF voltage=35V package="200 mil [THT, electrolytic]"]
  R2 = Resistor [tolerance=±5% resistance=10k power=0.25W package=THT]
  R1 = Resistor [tolerance=±5% resistance=10k power=0.25W package=THT]
  D2 = Schottky Diode [part_number=1N5819 package="300 mil [THT]"]
  R3 = Resistor [tolerance=±5% resistance=100 power=0.25W package=THT]
  D1 = Schottky Diode [part_number=1N5817 package="300 mil [THT]"]
  D4 = Schottky Diode [part_number=1N5817 package="300 mil [THT]"]
  D3 = Schottky Diode [part_number=1N5817 package="300 mil [THT]"]
  Pad4 = Pad [width=7.472466910769734 height=17.81152607440313 connect=center]
  Pad3 = Pad [width=7.902222222222222 height=9.03111111111111 connect=center]
  Pad2 = Pad [width=7.902222222222222 height=9.03111111111111 connect=center]
  Pad1 = Pad [width=7.902222222222222 height=9.03111111111111 connect=center]

nets:
  N1: Q1.gate, R2.Pin_1
  N2: Q1.drain, D1.cathode, D4.cathode, D3.anode, Pad3.pad
  N3: Q1.source, D2.cathode
  N4: V1.V+, R2.Pin_0, R1.Pin_1, D1.anode, Pad1.pad
  GND: V1.V-, V2.V-, C1.-, R1.Pin_0, Pad4.pad
  N5: V2.V+, D2.anode, Pad2.pad
  N6: C1.+, R3.Pin_1, D4.anode
  N7: R3.Pin_0, D3.cathode
