# Fritzing sketch Transistor (saved by Fritzing 1.0.2b)
breadboards: 1

parts:
  A1 = Arduino UNO R4 WiFi
  LED1 = smd LED [color="Red (633nm)" package="0805 [SMD]"]
  R1 = Resistor [tolerance=±5% resistance=220 package="2010 [SMD]"]
  R2 = Resistor [tolerance=±5% resistance=10k package="2010 [SMD]"]
  Q1 = TRANSISTOR_NPN [package=to-92]

nets:
  N1: A1.Pin_8, A1.Pin_27, Q1.C
  N2: A1.Pin_9, A1.Pin_18, LED1.cathode
  N3: A1.Pin_42, R2.Pin_0
  N4: LED1.anode, R1.Pin_1
  N5: R1.Pin_0, Q1.E
  N6: R2.Pin_1, Q1.B

custom parts:
  Arduino UNO R4 WiFi: The Arduino UNO R4 WiFi merges the RA4M1 microprocessor from Renesas with the ESP32-S3 from Espressif, creating an all-in-one tool for makers with enhanced processing power and a diverse array of new peripherals.
