# Fritzing sketch PHT Sensor (saved by Fritzing 1.0.2b)

parts:
  Part1 = Adafruit MS8607 PHT Sensor [part_number="Adafruit #4716"]
  Part2 = Arduino Uno (Rev3)

nets:
  VCC: Part1.VCC, Part2.3V3
  GND: Part1.GND, Part2.GND
  N1: Part1.SCL, Part2.A5/SCL
  N2: Part1.SDA, Part2.A4/SDA

custom parts:
  Adafruit MS8607 PHT Sensor: Because of their many applications, Pressure, Temperature, and Humidity sensors (PHT sensors) are a common offering from semiconductor companies. The MS8607 PHT sensor from TE Connectivity does an admirable job of measuring a wide range of all three environmental conditions. Each and every MS8607 sensor is calibrated at the factory and the calibration constants stored in the sensor itself.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
