# Fritzing sketch client power (saved by Fritzing 1.0.2b)

parts:
  A1 = Arduino UNO R4 WiFi
  SPDT_Switch = Taiway 100-SP-X-T1 SPDT Miniature Toggle Switch [part_number=100-SP-X-T1-0-0-B1-M1 package=THT]
  9_Volt = BC9VPC [package=bc9vpc]
  Barrel_Plug = Power Jack [package=power_jack_pth_lock]

nets:
  N1: A1.Pin_9, A1.Pin_30, A1.Pin_48, 9_Volt.V-, Barrel_Plug.GND, Barrel_Plug.GNDBREAK
  N2: A1.Pin_11, SPDT_Switch.COM
  N3: SPDT_Switch.L1, 9_Volt.V+
  N4: SPDT_Switch.L2, Barrel_Plug.PWR

custom parts:
  Arduino UNO R4 WiFi: The Arduino UNO R4 WiFi merges the RA4M1 microprocessor from Renesas with the ESP32-S3 from Espressif, creating an all-in-one tool for makers with enhanced processing power and a diverse array of new peripherals.
