# Fritzing sketch RFM69HCW (saved by Fritzing 1.0.2b)

parts:
  Part1 = Adafruit RFM69HCW Transceiver Radio [part_number="Adafruit #3070 and #3071"]
  A1 = Arduino UNO R4 WiFi
  U1 = U.FL [package=u.fl]

nets:
  N1: Part1.ANTENNA, U1.SIGNAL
  N2: Part1.VIN, A1.Pin_8, A1.Pin_27
  N3: Part1.GND, A1.Pin_2, A1.Pin_48
  N4: Part1.DIO0, A1.Pin_37
  N5: Part1.SCK, A1.Pin_47
  N6: Part1.MISO, A1.Pin_46
  N7: Part1.MOSI, A1.Pin_45
  N8: Part1.CS, A1.Pin_38
  N9: Part1.RST, A1.Pin_36

custom parts:
  Adafruit RFM69HCW Transceiver Radio: Sending data over long distances is like magic, and now you can be a magician with this range of powerful and easy-to-use radio modules. Sure, sometimes you want to talk to a computer (a good time to use WiFi) or perhaps communicate with a Phone (choose Bluetooth Low Energy!) but what if you want to send data very far? Most WiFi, Bluetooth, Zigbee and other wireless chipsets use 2.4GHz, which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
  Arduino UNO R4 WiFi: The Arduino UNO R4 WiFi merges the RA4M1 microprocessor from Renesas with the ESP32-S3 from Espressif, creating an all-in-one tool for makers with enhanced processing power and a diverse array of new peripherals.
